// Digital circuit add_5bit.dig as structural Verilog
module add_5bit (
  input  [4:0] a,
  input  [4:0] b,
  input  sub,
  output [4:0] out,
  output cout
);

  wire add_1bit_1_cout, add_1bit_2_cout, add_1bit_3_cout, add_1bit_4_cout;
  wire [4:0] xor_1_out;

  assign xor_1_out = b ^ {5{sub}};  // XOr xor_1, 5 bits wide
  add_1bit add_1bit_1 (.a(a[0]), .b(xor_1_out[0]), .cin(sub), .out(out[0]), .cout(add_1bit_1_cout));
  add_1bit add_1bit_2 (.a(a[1]), .b(xor_1_out[1]), .cin(add_1bit_1_cout), .out(out[1]), .cout(add_1bit_2_cout));
  add_1bit add_1bit_3 (.a(a[2]), .b(xor_1_out[2]), .cin(add_1bit_2_cout), .out(out[2]), .cout(add_1bit_3_cout));
  add_1bit add_1bit_4 (.a(a[3]), .b(xor_1_out[3]), .cin(add_1bit_3_cout), .out(out[3]), .cout(add_1bit_4_cout));
  add_1bit add_1bit_5 (.a(a[4]), .b(xor_1_out[4]), .cin(add_1bit_4_cout), .out(out[4]), .cout(cout));
endmodule
