// Digital circuit addsub_5bit.dig as structural Verilog
module addsub_5bit (
  input  [4:0] a,
  input  [4:0] b,
  output [4:0] out,
  output cout
);

  wire add_1bit_1_cout, add_1bit_2_cout, add_1bit_3_cout, add_1bit_4_cout;

  add_1bit add_1bit_1 (.a(a[0]), .b(b[0]), .cin(1'b0), .out(out[0]), .cout(add_1bit_1_cout));
  add_1bit add_1bit_2 (.a(a[1]), .b(b[1]), .cin(add_1bit_1_cout), .out(out[1]), .cout(add_1bit_2_cout));
  add_1bit add_1bit_3 (.a(a[2]), .b(b[2]), .cin(add_1bit_2_cout), .out(out[2]), .cout(add_1bit_3_cout));
  add_1bit add_1bit_4 (.a(a[3]), .b(b[3]), .cin(add_1bit_3_cout), .out(out[3]), .cout(add_1bit_4_cout));
  add_1bit add_1bit_5 (.a(a[4]), .b(b[4]), .cin(add_1bit_4_cout), .out(out[4]), .cout(cout));
endmodule
