// Digital circuit exp_calc.dig as structural Verilog
module exp_calc (
  input  [4:0] a,
  input  [4:0] b,
  output [4:0] out
);

  wire [4:0] add_5bit_1_out;

  add_5bit add_5bit_1 (.a(a), .b(b), .sub(1'b0), .out(add_5bit_1_out));  // open: cout
  add_5bit add_5bit_2 (.a(add_5bit_1_out), .b(5'b01111), .sub(1'b1), .out(out));  // open: cout
endmodule
