// Digital circuit matmul.dig as structural Verilog
module matmul (
  input  clk,
  input  [63:0] b,
  input  [63:0] a,
  output [63:0] out,
  output [15:0] out_5
);

  exp_calc exp_calc_1 (.a(a[5:1]), .b(b[5:1]), .out(out_5[5:1]));

  assign out = b;
endmodule
