// Digital circuit decoder.dig as structural Verilog
module decoder (
  input  [31:0] instruction,
  output [3:0] opcode,
  output [2:0] rd,
  output [2:0] rs,
  output [5:0] funct,
  output [15:0] imm
);

  // Pins of 5 and 6 bits meet at instruction[21:16]

  assign funct = instruction[21:16];
  assign imm = instruction[15:0];
  assign opcode = instruction[31:28];
  assign rd = instruction[27:25];
  assign rs = instruction[24:22];
endmodule
