// Digital circuit main.dig as structural Verilog
module main (
  input  clk,
  output [3:0] out_2,
  output [3:0] out_3,
  output [15:0] out_4,
  output [15:0] out_5,
  output [15:0] out_6,
  output [15:0] out_7,
  output [15:0] out_8,
  output [15:0] out_9,
  output [15:0] out_10,
  output [15:0] out_11,
  output [15:0] out_12,
  output [15:0] out_13,
  output [15:0] out_14,
  output [15:0] out_15,
  output [15:0] out_16,
  output [15:0] out_17,
  output [15:0] out_18,
  output [15:0] out_19
);

  wire d_flip_flop_2_q, demultiplexer_1_out_0, demultiplexer_1_out_1, demultiplexer_1_out_2,
       demultiplexer_1_out_3, demultiplexer_1_out_4, demultiplexer_1_out_5, demultiplexer_1_out_6,
       demultiplexer_1_out_7, not_1_out;
  wire [2:0] decoder_1_rd;
  wire [12:0] add_1_s, d_flip_flop_1_q;
  wire [31:0] rom_1_d;

  d_flip_flop #(.generic("bitWidth := 13;")) d_flip_flop_1 (
    .in(d_flip_flop_2_q), .clk(clk), .Q(d_flip_flop_1_q));  // open: Q_2
  Add #(.Bits(13)) add_1 (.a(13'h1), .b(d_flip_flop_1_q), .c_i(clk), .s(add_1_s));  // open: c_o
  not not_1 (not_1_out, clk);
  d_flip_flop #(.generic("bitWidth := 13;")) d_flip_flop_2 (
    .in(add_1_s), .clk(not_1_out), .Q(d_flip_flop_2_q));  // open: Q_2
  ROM #(.bigEndian("true"), .AddrBits(13), .Bits(32)) rom_1 (.A(d_flip_flop_1_q), .sel(1'b1), .D(rom_1_d));
  decoder decoder_1 (.instruction(rom_1_d), .opcode(out_3), .rd(decoder_1_rd));  // open: rs, funct, imm
  Demultiplexer #(.Selector_Bits(3)) demultiplexer_1 (
    .sel(decoder_1_rd), .in(1'b1), .out_0(demultiplexer_1_out_0), .out_1(demultiplexer_1_out_1),
    .out_2(demultiplexer_1_out_2), .out_3(demultiplexer_1_out_3), .out_4(demultiplexer_1_out_4),
    .out_5(demultiplexer_1_out_5), .out_6(demultiplexer_1_out_6), .out_7(demultiplexer_1_out_7));
  assign out_2 = ~(4'b0000 ^ out_3);  // XNOr xnor_1, 4 bits wide
  register #(.generic("bitWidth := 16;")) register_1 (
    .in(16'h1), .clk(clk), .en(demultiplexer_1_out_0), .Q(out_4), .Q_2(out_5));
  register #(.generic("bitWidth := 16;")) register_2 (
    .in(16'h1), .clk(clk), .en(demultiplexer_1_out_1), .Q(out_6), .Q_2(out_7));
  register #(.generic("bitWidth := 16;")) register_3 (
    .in(16'h1), .clk(clk), .en(demultiplexer_1_out_2), .Q(out_8), .Q_2(out_9));
  register #(.generic("bitWidth := 16;")) register_4 (
    .in(16'h1), .clk(clk), .en(demultiplexer_1_out_3), .Q(out_10), .Q_2(out_11));
  register #(.generic("bitWidth := 16;")) register_5 (
    .in(16'h1), .clk(clk), .en(demultiplexer_1_out_4), .Q(out_12), .Q_2(out_13));
  register #(.generic("bitWidth := 16;")) register_6 (
    .in(16'h1), .clk(clk), .en(demultiplexer_1_out_5), .Q(out_14), .Q_2(out_15));
  register #(.generic("bitWidth := 16;")) register_7 (
    .in(16'h1), .clk(clk), .en(demultiplexer_1_out_6), .Q(out_16), .Q_2(out_17));
  register #(.generic("bitWidth := 16;")) register_8 (
    .in(16'h1), .clk(clk), .en(demultiplexer_1_out_7), .Q(out_18), .Q_2(out_19));

  // Notes on the sheet:
  //   rom_1 loads program
endmodule
