// Digital circuit d_flip_flop.dig as structural Verilog
module d_flip_flop (
  input  in,
  input  clk,
  output Q,
  output Q_2
);

  wire bitextender_1_out, nand_1_out, nand_2_out, not_1_out;

  not not_1 (not_1_out, in);
  BitExtender #(.inputBits(1), .outputBits(1), .generic("this.outputBits = args.bitWidth;")) bitextender_1 (
    .in(clk), .out(bitextender_1_out));
  nand nand_1 (nand_1_out, in, bitextender_1_out);
  nand nand_2 (nand_2_out, bitextender_1_out, not_1_out);
  nand nand_3 (Q, nand_1_out, Q_2);
  nand nand_4 (Q_2, Q, nand_2_out);
endmodule

/* Code that sets the parameters or builds the circuit:
bitWidth := 13;
*/
