// Digital circuit register.dig as structural Verilog
module register (
  input  in,
  input  clk,
  input  en,
  output Q,
  output Q_2
);

  wire and_1_out;

  and and_1 (and_1_out, clk, en);
  d_flip_flop #(.generic("bitWidth := args.bitWidth;")) d_flip_flop_1 (.in(in), .clk(and_1_out), .Q(Q), .Q_2(Q_2));
endmodule

/* Code that sets the parameters or builds the circuit:
bitWidth := 16;
*/
